# Fritzing sketch raspirepcol (saved by Fritzing 0.7.7b)
breadboards: 1

parts:
  Raspberry_Pi1 = Raspberry Pi (Model B)
  S1 = Pushbutton [package="[THT]"]
  S2 = Pushbutton [package="[THT]"]
  S3 = Pushbutton [package="[THT]"]
  S4 = Pushbutton [package="[THT]"]
  R1 = Resistor [tolerance=±5% resistance=1k package=THT]
  R2 = Resistor [tolerance=±5% resistance=1k package=THT]
  R3 = Resistor [tolerance=±5% resistance=1k package=THT]
  R4 = Resistor [tolerance=±5% resistance=1k package=THT]
  R5 = Resistor [tolerance=±5% resistance=10k package=THT]
  R6 = Resistor [tolerance=±5% resistance=10k package=THT]
  R7 = Resistor [tolerance=±5% resistance=10k package=THT]
  R8 = Resistor [tolerance=±5% resistance=10k package=THT]
  R9 = Resistor [tolerance=±5% resistance=330 package=THT]
  R10 = Resistor [tolerance=±5% resistance=330 package=THT]
  R11 = Resistor [tolerance=±5% resistance=330 package=THT]
  R12 = Resistor [tolerance=±5% resistance=330 package=THT]
  LED1 = LED - 5mm [color="Red (633nm)" package="5 mm [THT]"]
  LED2 = LED - 5mm [color="Green (555nm)" package="5 mm [THT]"]
  LED3 = LED - 5mm [color="Yellow (585nm)" package="5 mm [THT]"]
  LED4 = LED - 5mm [color="Blue (470nm)" package="5 mm [THT]"]

nets:
  N1: Raspberry_Pi1.3V3, R5.Pin_1, R6.Pin_1, R7.Pin_1, R8.Pin_1
  N2: Raspberry_Pi1.GND, S1.Pin_3, S1.Pin_4, S2.Pin_3, S2.Pin_4, S3.Pin_3, S3.Pin_4, S4.Pin_3, S4.Pin_4, LED1.cathode, LED2.cathode, LED3.cathode, LED4.cathode
  N3: Raspberry_Pi1.#4, R9.Pin_1
  N4: Raspberry_Pi1.#17, R10.Pin_1
  N5: Raspberry_Pi1.#18, R11.Pin_1
  N6: Raspberry_Pi1.#21, R12.Pin_1
  N7: Raspberry_Pi1.#22, R4.Pin_0
  N8: Raspberry_Pi1.#23, R3.Pin_0
  N9: Raspberry_Pi1.#24, R2.Pin_0
  N10: Raspberry_Pi1.#25, R1.Pin_0
  N11: S1.Pin_1, S1.Pin_2, R4.Pin_1, R8.Pin_0
  N12: S2.Pin_1, S2.Pin_2, R3.Pin_1, R7.Pin_0
  N13: S3.Pin_1, S3.Pin_2, R2.Pin_1, R6.Pin_0
  N14: S4.Pin_1, S4.Pin_2, R1.Pin_1, R5.Pin_0
  N15: R9.Pin_0, LED1.anode
  N16: R10.Pin_0, LED2.anode
  N17: R11.Pin_0, LED3.anode
  N18: R12.Pin_0, LED4.anode

custom parts:
  Raspberry Pi (Model B): Raspberry Pi Single-board Computer, Model B
